// Digital circuit labtimer.dig as structural Verilog
module labtimer (
  input  CLK,
  input  SW,
  input  B3,
  input  B2,
  input  B1,
  input  B0,
  input  HZ1,
  output [3:0] M10,
  output [3:0] M1,
  output [3:0] S10,
  output [3:0] S1
);

  wire and_1_out, and_2_out, and_3_out, and_4_out, and_5_out, and_6_out, and_7_out, and_8_out, and_9_out,
       and_10_out, and_11_out, and_12_out, and_13_out, and_14_out, and_15_out, and_16_out, and_17_out,
       and_18_out, and_19_out, and_20_out, and_21_out, and_22_out, and_23_out, and_24_out, and_25_out,
       and_26_out, and_27_out, and_28_out, and_29_out, and_30_out, and_31_out, and_32_out, and_33_out,
       and_34_out, and_35_out, and_36_out, and_37_out, and_38_out, and_39_out, and_40_out, and_41_out,
       and_42_out, and_43_out, and_44_out, and_45_out, and_46_out, and_47_out, and_48_out, and_49_out,
       and_50_out, and_51_out, and_52_out, and_53_out, and_54_out, and_55_out, and_56_out, and_57_out,
       and_58_out, and_59_out, and_60_out, and_61_out, and_62_out, and_63_out, and_64_out, and_65_out,
       and_66_out, and_67_out, and_68_out, and_69_out, and_70_out, and_71_out, and_72_out, and_73_out,
       and_74_out, and_75_out, and_76_out, and_77_out, and_78_out, and_79_out, and_80_out, and_81_out,
       and_82_out, and_83_out, and_84_out, and_85_out, and_86_out, and_87_out, and_88_out, and_89_out,
       and_90_out, and_91_out, and_92_out, and_93_out, and_94_out, and_95_out, and_96_out, d_ff_2_nq,
       d_ff_3_nq, d_ff_4_nq, d_ff_5_nq, d_ff_6_nq, d_ff_7_nq, d_ff_8_nq, d_ff_9_q, d_ff_10_q, d_ff_11_q,
       d_ff_12_q, d_ff_13_q, d_ff_14_nq, d_ff_15_nq, d_ff_16_nq, d_ff_17_nq, d_ff_18_nq, d_ff_19_nq,
       d_ff_20_nq, d_ff_21_nq, multiplexer_1_out, multiplexer_2_out, multiplexer_3_out, multiplexer_4_out,
       multiplexer_5_out, multiplexer_6_out, multiplexer_7_out, multiplexer_8_out, multiplexer_9_out,
       multiplexer_10_out, multiplexer_11_out, multiplexer_12_out, multiplexer_13_out, multiplexer_14_out,
       multiplexer_15_out, multiplexer_16_out, multiplexer_17_out, multiplexer_18_out, multiplexer_19_out,
       multiplexer_20_out, multiplexer_21_out, multiplexer_22_out, multiplexer_23_out, multiplexer_24_out,
       multiplexer_25_out, multiplexer_26_out, multiplexer_27_out, multiplexer_28_out, multiplexer_29_out,
       multiplexer_30_out, multiplexer_31_out, multiplexer_32_out, multiplexer_33_out, multiplexer_34_out,
       multiplexer_35_out, multiplexer_36_out, multiplexer_37_out, multiplexer_38_out, multiplexer_39_out,
       multiplexer_40_out, multiplexer_41_out, multiplexer_42_out, multiplexer_43_out, multiplexer_44_out,
       multiplexer_45_out, multiplexer_46_out, multiplexer_47_out, multiplexer_48_out, multiplexer_49_out,
       multiplexer_50_out, multiplexer_51_out, multiplexer_52_out, multiplexer_53_out, multiplexer_54_out,
       multiplexer_55_out, multiplexer_56_out, multiplexer_57_out, multiplexer_58_out, multiplexer_59_out,
       multiplexer_60_out, multiplexer_61_out, multiplexer_62_out, multiplexer_63_out, multiplexer_64_out,
       nor_1_out, nor_2_out, nor_3_out, nor_4_out, not_1_out, not_2_out, not_3_out, not_4_out, not_5_out,
       not_6_out, not_7_out, not_8_out, not_9_out, not_10_out, not_11_out, not_12_out, not_13_out,
       not_14_out, not_15_out, not_16_out, not_17_out, or_1_out, or_2_out, or_3_out, or_4_out, or_5_out,
       or_6_out, or_7_out, or_8_out, or_9_out, or_10_out, or_11_out, or_12_out, or_13_out, or_14_out,
       or_15_out, or_16_out, or_17_out, or_18_out, or_19_out, or_20_out, or_21_out, or_22_out, or_23_out,
       or_24_out, or_25_out, or_26_out, or_27_out, or_28_out, or_29_out, or_30_out, or_31_out, or_32_out,
       or_33_out, or_34_out, or_35_out, or_36_out, or_37_out, or_38_out, or_39_out, or_41_out, xor_1_out,
       xor_2_out, xor_3_out;

  and and_1 (and_1_out, d_ff_4_nq, d_ff_3_nq, S10[0]);
  and and_2 (and_2_out, d_ff_4_nq, S10[1], d_ff_2_nq);
  and and_3 (and_3_out, d_ff_4_nq, S10[1], S10[0]);
  and and_4 (and_4_out, S10[2], d_ff_3_nq, d_ff_2_nq);
  or or_1 (or_1_out, and_1_out, and_2_out);
  or or_2 (or_2_out, and_3_out, and_4_out);
  xor xor_1 (xor_1_out, M1[1], and_5_out);
  and and_5 (and_5_out, M1[0], d_ff_8_nq);
  and and_6 (and_6_out, d_ff_7_nq, M1[1], M1[0]);
  and and_7 (and_7_out, M1[2], d_ff_6_nq);
  and and_8 (and_8_out, M1[2], d_ff_5_nq);
  and and_9 (and_9_out, M1[2], M1[1], M1[0]);
  and and_10 (and_10_out, M1[3], d_ff_5_nq);
  Multiplexer multiplexer_1 (.sel(and_54_out), .in_0(S10[0]), .in_1(d_ff_2_nq), .out(multiplexer_1_out));
  Multiplexer multiplexer_2 (.sel(and_54_out), .in_0(S10[1]), .in_1(or_1_out), .out(multiplexer_2_out));
  Multiplexer multiplexer_3 (.sel(and_54_out), .in_0(S10[2]), .in_1(or_2_out), .out(multiplexer_3_out));
  Multiplexer multiplexer_4 (.sel(and_54_out), .in_0(S10[3]), .in_1(1'b0), .out(multiplexer_4_out));
  or or_3 (or_3_out, and_6_out, and_7_out, and_8_out);
  or or_4 (or_4_out, and_9_out, and_10_out);
  Multiplexer multiplexer_5 (.sel(and_53_out), .in_0(M1[0]), .in_1(d_ff_5_nq), .out(multiplexer_5_out));
  Multiplexer multiplexer_6 (.sel(and_53_out), .in_0(M1[1]), .in_1(xor_1_out), .out(multiplexer_6_out));
  Multiplexer multiplexer_7 (.sel(and_53_out), .in_0(M1[2]), .in_1(or_3_out), .out(multiplexer_7_out));
  Multiplexer multiplexer_8 (.sel(and_53_out), .in_0(M1[3]), .in_1(or_4_out), .out(multiplexer_8_out));
  and and_11 (and_11_out, S10[0], S10[2]);
  and and_12 (and_12_out, d_ff_2_nq, d_ff_3_nq, d_ff_4_nq);
  and and_13 (and_13_out, M1[3], d_ff_5_nq);
  and and_14 (and_14_out, M1[0], M1[1], M1[2]);
  or or_5 (or_5_out, and_14_out, and_13_out);
  and and_15 (and_15_out, S10[0], S10[1]);
  and and_16 (and_16_out, d_ff_2_nq, S10[2]);
  or or_6 (or_6_out, and_11_out, and_12_out);
  or or_7 (or_7_out, and_15_out, and_16_out);
  and and_17 (and_17_out, d_ff_7_nq, M1[1], M1[0]);
  and and_18 (and_18_out, d_ff_6_nq, M1[2]);
  and and_19 (and_19_out, M1[2], d_ff_5_nq);
  Multiplexer multiplexer_9 (.sel(d_ff_13_q), .in_0(1'b0), .in_1(1'b0), .out(multiplexer_9_out));
  or or_8 (or_8_out, and_17_out, and_18_out, and_19_out);
  and and_20 (and_20_out, M1[0], M1[1]);
  and and_21 (and_21_out, M1[3], d_ff_5_nq);
  and and_22 (and_22_out, d_ff_5_nq, M1[2], d_ff_6_nq);
  and and_23 (and_23_out, M1[0], M1[3]);
  and and_24 (and_24_out, d_ff_5_nq, d_ff_6_nq, d_ff_7_nq, d_ff_8_nq);
  and and_25 (and_25_out, d_ff_2_nq, S10[1]);
  and and_26 (and_26_out, S10[0], d_ff_3_nq, d_ff_4_nq);
  and and_27 (and_27_out, S10[0], S10[1]);
  and and_28 (and_28_out, S10[2], d_ff_2_nq);
  Multiplexer multiplexer_10 (.sel(or_26_out), .in_0(S10[3]), .in_1(multiplexer_9_out), .out(multiplexer_10_out));
  or or_9 (or_9_out, and_25_out, and_26_out);
  and and_29 (and_29_out, M1[3], d_ff_5_nq);
  and and_30 (and_30_out, M1[1], M1[2]);
  and and_31 (and_31_out, M1[2], M1[0]);
  and and_32 (and_32_out, M1[0], d_ff_6_nq, d_ff_8_nq);
  and and_33 (and_33_out, d_ff_5_nq, M1[1]);
  or or_10 (or_10_out, and_20_out, and_21_out, and_22_out);
  Multiplexer multiplexer_11 (.sel(d_ff_13_q), .in_0(d_ff_2_nq), .in_1(d_ff_2_nq), .out(multiplexer_11_out));
  Multiplexer multiplexer_12 (.sel(d_ff_13_q), .in_0(or_7_out), .in_1(or_9_out), .out(multiplexer_12_out));
  Multiplexer multiplexer_13 (.sel(d_ff_13_q), .in_0(or_6_out), .in_1(or_11_out), .out(multiplexer_13_out));
  or or_11 (or_11_out, and_28_out, and_27_out);
  D_FF d_ff_1 (.D(multiplexer_32_out), .C(CLK), .Q(S10[3]));  // open: nQ
  or or_12 (or_12_out, and_23_out, and_24_out);
  or or_13 (or_13_out, and_29_out, and_30_out, and_31_out);
  or or_14 (or_14_out, and_32_out, and_33_out);
  Multiplexer multiplexer_14 (.sel(d_ff_13_q), .in_0(d_ff_5_nq), .in_1(d_ff_5_nq), .out(multiplexer_14_out));
  Multiplexer multiplexer_15 (.sel(d_ff_13_q), .in_0(or_10_out), .in_1(or_14_out), .out(multiplexer_15_out));
  Multiplexer multiplexer_16 (.sel(d_ff_13_q), .in_0(or_13_out), .in_1(or_8_out), .out(multiplexer_16_out));
  Multiplexer multiplexer_17 (.sel(d_ff_13_q), .in_0(or_12_out), .in_1(or_5_out), .out(multiplexer_17_out));
  Multiplexer multiplexer_18 (.sel(or_26_out), .in_0(S10[0]), .in_1(multiplexer_11_out), .out(multiplexer_18_out));
  Multiplexer multiplexer_19 (.sel(or_26_out), .in_0(S10[1]), .in_1(multiplexer_12_out), .out(multiplexer_19_out));
  Multiplexer multiplexer_20 (.sel(or_26_out), .in_0(S10[2]), .in_1(multiplexer_13_out), .out(multiplexer_20_out));
  or or_15 (or_15_out, and_36_out, and_34_out);
  Multiplexer multiplexer_21 (.sel(SW), .in_0(multiplexer_18_out), .in_1(multiplexer_1_out), .out(multiplexer_21_out));
  Multiplexer multiplexer_22 (.sel(SW), .in_0(multiplexer_19_out), .in_1(multiplexer_2_out), .out(multiplexer_22_out));
  Multiplexer multiplexer_23 (.sel(SW), .in_0(multiplexer_20_out), .in_1(multiplexer_3_out), .out(multiplexer_23_out));
  and and_34 (and_34_out, d_ff_13_q, or_16_out, and_35_out);
  Multiplexer multiplexer_24 (.sel(SW), .in_0(multiplexer_28_out), .in_1(multiplexer_5_out), .out(multiplexer_24_out));
  Multiplexer multiplexer_25 (.sel(SW), .in_0(multiplexer_29_out), .in_1(multiplexer_6_out), .out(multiplexer_25_out));
  Multiplexer multiplexer_26 (.sel(SW), .in_0(multiplexer_30_out), .in_1(multiplexer_7_out), .out(multiplexer_26_out));
  Multiplexer multiplexer_27 (.sel(SW), .in_0(multiplexer_31_out), .in_1(multiplexer_8_out), .out(multiplexer_27_out));
  Multiplexer multiplexer_28 (.sel(or_16_out), .in_0(M1[0]), .in_1(multiplexer_14_out), .out(multiplexer_28_out));
  Multiplexer multiplexer_29 (.sel(or_16_out), .in_0(M1[1]), .in_1(multiplexer_15_out), .out(multiplexer_29_out));
  Multiplexer multiplexer_30 (.sel(or_16_out), .in_0(M1[2]), .in_1(multiplexer_16_out), .out(multiplexer_30_out));
  Multiplexer multiplexer_31 (.sel(or_16_out), .in_0(M1[3]), .in_1(multiplexer_17_out), .out(multiplexer_31_out));
  nor nor_1 (nor_1_out, M1[3], M1[2], M1[1], M1[0]);
  Multiplexer multiplexer_32 (.sel(SW), .in_0(multiplexer_10_out), .in_1(multiplexer_4_out), .out(multiplexer_32_out));
  D_FF d_ff_2 (.D(multiplexer_21_out), .C(CLK), .Q(S10[0]), .nQ(d_ff_2_nq));
  D_FF d_ff_3 (.D(multiplexer_22_out), .C(CLK), .Q(S10[1]), .nQ(d_ff_3_nq));
  D_FF d_ff_4 (.D(multiplexer_23_out), .C(CLK), .Q(S10[2]), .nQ(d_ff_4_nq));
  and and_35 (and_35_out, M1[3], not_2_out, not_1_out, M1[0]);
  and and_36 (and_36_out, nor_1_out, not_5_out, or_16_out);
  D_FF d_ff_5 (.D(multiplexer_24_out), .C(CLK), .Q(M1[0]), .nQ(d_ff_5_nq));
  D_FF d_ff_6 (.D(multiplexer_25_out), .C(CLK), .Q(M1[1]), .nQ(d_ff_6_nq));
  D_FF d_ff_7 (.D(multiplexer_26_out), .C(CLK), .Q(M1[2]), .nQ(d_ff_7_nq));
  D_FF d_ff_8 (.D(multiplexer_27_out), .C(CLK), .Q(M1[3]), .nQ(d_ff_8_nq));
  not not_1 (not_1_out, M1[1]);
  not not_2 (not_2_out, M1[2]);
  not not_3 (not_3_out, S10[3]);
  nor nor_2 (nor_2_out, S10[0], S10[1], S10[2], S10[3]);
  not not_4 (not_4_out, S10[1]);
  and and_37 (and_37_out, S10[0], S10[2], not_4_out, not_3_out);
  not not_5 (not_5_out, d_ff_13_q);
  and and_38 (and_38_out, nor_2_out, or_26_out, not_6_out);
  and and_39 (and_39_out, and_37_out, or_26_out, d_ff_13_q);
  not not_6 (not_6_out, d_ff_13_q);
  xor xor_2 (xor_2_out, S1[1], and_40_out);
  and and_40 (and_40_out, S1[0], d_ff_17_nq);
  and and_41 (and_41_out, d_ff_16_nq, S1[1], S1[0]);
  and and_42 (and_42_out, S1[2], d_ff_15_nq);
  and and_43 (and_43_out, S1[2], d_ff_14_nq);
  and and_44 (and_44_out, S1[2], S1[1], S1[0]);
  and and_45 (and_45_out, S1[3], d_ff_14_nq);
  or or_16 (or_16_out, and_38_out, and_39_out);
  or or_17 (or_17_out, and_41_out, and_42_out, and_43_out);
  or or_18 (or_18_out, and_44_out, and_45_out);
  Multiplexer multiplexer_33 (.sel(and_55_out), .in_0(S1[0]), .in_1(d_ff_14_nq), .out(multiplexer_33_out));
  Multiplexer multiplexer_34 (.sel(and_55_out), .in_0(S1[1]), .in_1(xor_2_out), .out(multiplexer_34_out));
  Multiplexer multiplexer_35 (.sel(and_55_out), .in_0(S1[2]), .in_1(or_17_out), .out(multiplexer_35_out));
  Multiplexer multiplexer_36 (.sel(and_55_out), .in_0(S1[3]), .in_1(or_18_out), .out(multiplexer_36_out));
  not not_7 (not_7_out, B3);
  D_FF d_ff_9 (.D(B3), .C(CLK), .Q(d_ff_9_q));  // open: nQ
  not not_8 (not_8_out, B2);
  D_FF d_ff_10 (.D(B2), .C(CLK), .Q(d_ff_10_q));  // open: nQ
  not not_9 (not_9_out, B1);
  D_FF d_ff_11 (.D(B1), .C(CLK), .Q(d_ff_11_q));  // open: nQ
  not not_10 (not_10_out, B0);
  D_FF d_ff_12 (.D(B0), .C(CLK), .Q(d_ff_12_q));  // open: nQ
  and and_46 (and_46_out, S1[3], d_ff_14_nq);
  and and_47 (and_47_out, S1[0], S1[1], S1[2]);
  or or_19 (or_19_out, and_47_out, and_46_out);
  and and_48 (and_48_out, not_7_out, d_ff_9_q);
  and and_49 (and_49_out, not_8_out, d_ff_10_q);
  and and_50 (and_50_out, not_9_out, d_ff_11_q);
  and and_51 (and_51_out, not_10_out, d_ff_12_q);
  and and_52 (and_52_out, SW, and_48_out);
  and and_53 (and_53_out, SW, and_49_out);
  and and_54 (and_54_out, SW, and_50_out);
  and and_55 (and_55_out, SW, and_51_out);
  and and_56 (and_56_out, d_ff_16_nq, S1[1], S1[0]);
  and and_57 (and_57_out, d_ff_15_nq, S1[2]);
  and and_58 (and_58_out, S1[2], d_ff_14_nq);
  not not_11 (not_11_out, SW);
  or or_20 (or_20_out, and_56_out, and_57_out, and_58_out);
  and and_59 (and_59_out, S1[0], S1[1]);
  and and_60 (and_60_out, S1[3], d_ff_14_nq);
  and and_61 (and_61_out, d_ff_14_nq, S1[2], d_ff_15_nq);
  and and_62 (and_62_out, S1[0], S1[3]);
  and and_63 (and_63_out, d_ff_14_nq, d_ff_15_nq, d_ff_16_nq, d_ff_17_nq);
  and and_64 (and_64_out, not_11_out, or_21_out);
  or or_21 (or_21_out, not_15_out, d_ff_13_q);
  and and_65 (and_65_out, not_11_out, HZ1);
  and and_66 (and_66_out, S1[3], d_ff_14_nq);
  and and_67 (and_67_out, S1[1], S1[2]);
  and and_68 (and_68_out, S1[2], S1[0]);
  and and_69 (and_69_out, S1[0], d_ff_15_nq, d_ff_17_nq);
  and and_70 (and_70_out, d_ff_14_nq, S1[1]);
  or or_22 (or_22_out, and_59_out, and_60_out, and_61_out);
  D_FF d_ff_13 (.D(and_64_out), .C(CLK), .Q(d_ff_13_q));  // open: nQ
  or or_23 (or_23_out, and_62_out, and_63_out);
  or or_24 (or_24_out, and_66_out, and_67_out, and_68_out);
  or or_25 (or_25_out, and_69_out, and_70_out);
  Multiplexer multiplexer_37 (.sel(d_ff_13_q), .in_0(d_ff_14_nq), .in_1(d_ff_14_nq), .out(multiplexer_37_out));
  Multiplexer multiplexer_38 (.sel(d_ff_13_q), .in_0(or_22_out), .in_1(or_25_out), .out(multiplexer_38_out));
  Multiplexer multiplexer_39 (.sel(d_ff_13_q), .in_0(or_24_out), .in_1(or_20_out), .out(multiplexer_39_out));
  Multiplexer multiplexer_40 (.sel(d_ff_13_q), .in_0(or_23_out), .in_1(or_19_out), .out(multiplexer_40_out));
  or or_26 (or_26_out, and_73_out, and_71_out);
  and and_71 (and_71_out, d_ff_13_q, and_65_out, and_72_out);
  Multiplexer multiplexer_41 (.sel(SW), .in_0(multiplexer_45_out), .in_1(multiplexer_33_out), .out(multiplexer_41_out));
  Multiplexer multiplexer_42 (.sel(SW), .in_0(multiplexer_46_out), .in_1(multiplexer_34_out), .out(multiplexer_42_out));
  Multiplexer multiplexer_43 (.sel(SW), .in_0(multiplexer_47_out), .in_1(multiplexer_35_out), .out(multiplexer_43_out));
  Multiplexer multiplexer_44 (.sel(SW), .in_0(multiplexer_48_out), .in_1(multiplexer_36_out), .out(multiplexer_44_out));
  Multiplexer multiplexer_45 (.sel(and_65_out), .in_0(S1[0]), .in_1(multiplexer_37_out), .out(multiplexer_45_out));
  Multiplexer multiplexer_46 (.sel(and_65_out), .in_0(S1[1]), .in_1(multiplexer_38_out), .out(multiplexer_46_out));
  Multiplexer multiplexer_47 (.sel(and_65_out), .in_0(S1[2]), .in_1(multiplexer_39_out), .out(multiplexer_47_out));
  Multiplexer multiplexer_48 (.sel(and_65_out), .in_0(S1[3]), .in_1(multiplexer_40_out), .out(multiplexer_48_out));
  nor nor_3 (nor_3_out, S1[3], S1[2], S1[1], S1[0]);
  and and_72 (and_72_out, S1[3], not_13_out, not_12_out, S1[0]);
  and and_73 (and_73_out, nor_3_out, not_14_out, and_65_out);
  D_FF d_ff_14 (.D(multiplexer_41_out), .C(CLK), .Q(S1[0]), .nQ(d_ff_14_nq));
  D_FF d_ff_15 (.D(multiplexer_42_out), .C(CLK), .Q(S1[1]), .nQ(d_ff_15_nq));
  D_FF d_ff_16 (.D(multiplexer_43_out), .C(CLK), .Q(S1[2]), .nQ(d_ff_16_nq));
  D_FF d_ff_17 (.D(multiplexer_44_out), .C(CLK), .Q(S1[3]), .nQ(d_ff_17_nq));
  not not_12 (not_12_out, S1[1]);
  not not_13 (not_13_out, S1[2]);
  not not_14 (not_14_out, d_ff_13_q);
  xor xor_3 (xor_3_out, M10[1], and_74_out);
  and and_74 (and_74_out, M10[0], d_ff_21_nq);
  and and_75 (and_75_out, d_ff_20_nq, M10[1], M10[0]);
  and and_76 (and_76_out, M10[2], d_ff_19_nq);
  and and_77 (and_77_out, M10[2], d_ff_18_nq);
  and and_78 (and_78_out, M10[2], M10[1], M10[0]);
  and and_79 (and_79_out, M10[3], d_ff_18_nq);
  or or_27 (or_27_out, and_75_out, and_76_out, and_77_out);
  or or_28 (or_28_out, and_78_out, and_79_out);
  Multiplexer multiplexer_49 (.sel(and_52_out), .in_0(M10[0]), .in_1(d_ff_18_nq), .out(multiplexer_49_out));
  Multiplexer multiplexer_50 (.sel(and_52_out), .in_0(M10[1]), .in_1(xor_3_out), .out(multiplexer_50_out));
  Multiplexer multiplexer_51 (.sel(and_52_out), .in_0(M10[2]), .in_1(or_27_out), .out(multiplexer_51_out));
  Multiplexer multiplexer_52 (.sel(and_52_out), .in_0(M10[3]), .in_1(or_28_out), .out(multiplexer_52_out));
  and and_80 (and_80_out, M10[3], d_ff_18_nq);
  and and_81 (and_81_out, M10[0], M10[1], M10[2]);
  or or_29 (or_29_out, and_81_out, and_80_out);
  or or_30 (or_30_out, S1[0], S1[1], S1[2], S1[3]);
  or or_31 (or_31_out, S10[0], S10[1], S10[2], S10[3]);
  or or_32 (or_32_out, M1[0], M1[1], M1[2], M1[3]);
  or or_33 (or_33_out, M10[0], M10[1], M10[2], M10[3]);
  and and_82 (and_82_out, d_ff_20_nq, M10[1], M10[0]);
  and and_83 (and_83_out, d_ff_19_nq, M10[2]);
  and and_84 (and_84_out, M10[2], d_ff_18_nq);
  or or_34 (or_34_out, or_30_out, or_31_out, or_32_out, or_33_out);
  or or_35 (or_35_out, and_82_out, and_83_out, and_84_out);
  and and_85 (and_85_out, M10[0], M10[1]);
  and and_86 (and_86_out, M10[3], d_ff_18_nq);
  and and_87 (and_87_out, d_ff_18_nq, M10[2], d_ff_19_nq);
  and and_88 (and_88_out, M10[0], M10[3]);
  and and_89 (and_89_out, d_ff_18_nq, d_ff_19_nq, d_ff_20_nq, d_ff_21_nq);
  not not_15 (not_15_out, or_34_out);
  and and_90 (and_90_out, M10[3], d_ff_18_nq);
  and and_91 (and_91_out, M10[1], M10[2]);
  and and_92 (and_92_out, M10[2], M10[0]);
  and and_93 (and_93_out, M10[0], d_ff_19_nq, d_ff_21_nq);
  and and_94 (and_94_out, d_ff_18_nq, M10[1]);
  or or_36 (or_36_out, and_85_out, and_86_out, and_87_out);
  or or_37 (or_37_out, and_88_out, and_89_out);
  or or_38 (or_38_out, and_90_out, and_91_out, and_92_out);
  or or_39 (or_39_out, and_93_out, and_94_out);
  // Or or_40 has open pins: In_1=and_96_out, In_2=and_95_out, out=open
  Multiplexer multiplexer_53 (.sel(d_ff_13_q), .in_0(d_ff_18_nq), .in_1(d_ff_18_nq), .out(multiplexer_53_out));
  Multiplexer multiplexer_54 (.sel(d_ff_13_q), .in_0(or_36_out), .in_1(or_39_out), .out(multiplexer_54_out));
  Multiplexer multiplexer_55 (.sel(d_ff_13_q), .in_0(or_38_out), .in_1(or_35_out), .out(multiplexer_55_out));
  Multiplexer multiplexer_56 (.sel(d_ff_13_q), .in_0(or_37_out), .in_1(or_29_out), .out(multiplexer_56_out));
  Multiplexer multiplexer_57 (.sel(SW), .in_0(multiplexer_61_out), .in_1(multiplexer_49_out), .out(multiplexer_57_out));
  Multiplexer multiplexer_58 (.sel(SW), .in_0(multiplexer_62_out), .in_1(multiplexer_50_out), .out(multiplexer_58_out));
  Multiplexer multiplexer_59 (.sel(SW), .in_0(multiplexer_63_out), .in_1(multiplexer_51_out), .out(multiplexer_59_out));
  Multiplexer multiplexer_60 (.sel(SW), .in_0(multiplexer_64_out), .in_1(multiplexer_52_out), .out(multiplexer_60_out));
  and and_95 (and_95_out, or_41_out, or_15_out, or_41_out);
  nor nor_4 (nor_4_out, M10[3], M10[2], M10[1], M10[0]);
  Multiplexer multiplexer_61 (.sel(or_15_out), .in_0(M10[0]), .in_1(multiplexer_53_out), .out(multiplexer_61_out));
  Multiplexer multiplexer_62 (.sel(or_15_out), .in_0(M10[1]), .in_1(multiplexer_54_out), .out(multiplexer_62_out));
  Multiplexer multiplexer_63 (.sel(or_15_out), .in_0(M10[2]), .in_1(multiplexer_55_out), .out(multiplexer_63_out));
  Multiplexer multiplexer_64 (.sel(or_15_out), .in_0(M10[3]), .in_1(multiplexer_56_out), .out(multiplexer_64_out));
  or or_41 (or_41_out, not_17_out, M10[2], M10[1], not_16_out);
  and and_96 (and_96_out, nor_4_out, or_15_out, or_15_out);
  D_FF d_ff_18 (.D(multiplexer_57_out), .C(CLK), .Q(M10[0]), .nQ(d_ff_18_nq));
  D_FF d_ff_19 (.D(multiplexer_58_out), .C(CLK), .Q(M10[1]), .nQ(d_ff_19_nq));
  D_FF d_ff_20 (.D(multiplexer_59_out), .C(CLK), .Q(M10[2]), .nQ(d_ff_20_nq));
  D_FF d_ff_21 (.D(multiplexer_60_out), .C(CLK), .Q(M10[3]), .nQ(d_ff_21_nq));
  not not_16 (not_16_out, M10[0]);
  not not_17 (not_17_out, M10[3]);

  // Notes on the sheet:
  //   SW: default 1
endmodule
